// Digital circuit ALU.dig as structural Verilog
module ALU (
  input  [7:0] Data_In,
  input  Clk,
  input  A_In,
  input  B_In,
  input  Mode,
  output [7:0] A_Out,
  output [7:0] B_Out,
  output [7:0] Q,
  output Q_Bool
);

  wire [2:0] Mode_q;
  wire [7:0] add_1_s, and_1_out, barrelshifter_1_out, barrelshifter_2_out, multiplexer_1_out, or_1_out,
       sub_1_s;
  wire [7:7] comparator_1_eq, comparator_1_gt;

  Register #(.Bits(8)) A (.D(Data_In), .C(Clk), .en(A_In), .Q(A_Out));
  Register #(.Bits(8)) B (.D(Data_In), .C(Clk), .en(B_In), .Q(B_Out));
  Register #(.Bits(3)) u_Mode (.D(Data_In[2:0]), .C(Clk), .en(Mode), .Q(Mode_q));
  Add #(.Bits(8)) add_1 (.a(A_Out), .b(B_Out), .c_i(1'b0), .s(add_1_s));  // open: c_o
  Sub #(.Bits(8)) sub_1 (.a(A_Out), .b(B_Out), .c_i(1'b0), .s(sub_1_s));  // open: c_o
  Comparator #(.Bits(8)) comparator_1 (
    .a(A_Out), .b(B_Out), .gt(comparator_1_gt[7]), .eq(comparator_1_eq[7]));  // open: lt
  assign and_1_out = A_Out & B_Out;  // And and_1, 8 bits wide
  assign or_1_out = A_Out | B_Out;  // Or or_1, 8 bits wide
  BarrelShifter #(.Bits(8)) barrelshifter_1 (.in(A_Out), .shift(B_Out[3:0]), .out(barrelshifter_1_out));
  BarrelShifter #(.Bits(8), .direction("right")) barrelshifter_2 (
    .in(A_Out), .shift(B_Out[3:0]), .out(barrelshifter_2_out));
  Multiplexer #(.Bits(8)) multiplexer_1 (
    .sel(B_Out[4]), .in_0(barrelshifter_1_out), .in_1(barrelshifter_2_out), .out(multiplexer_1_out));
  Multiplexer #(.Selector_Bits(3), .Bits(8)) multiplexer_2 (
    .sel(Mode_q), .in_0(add_1_s), .in_1(sub_1_s), .in_2({8{comparator_1_gt[7]}}),
    .in_3({8{comparator_1_eq[7]}}), .in_4(and_1_out), .in_5(or_1_out), .in_6({8{1'b0}}),
    .in_7(multiplexer_1_out), .out(Q));
  or or_2 (Q_Bool, Q[0], Q[1], Q[2], Q[3], Q[4], Q[5], Q[6], Q[7]);
endmodule
