// Digital circuit CPU.dig as structural Verilog
module CPU (
  input  Slow,
  input  Fast
);

  wire and_2_out, and_3_out, and_4_out, and_5_out, AR_In, AR_Out, button_1_out, button_2_out, button_3_out,
       button_4_out, Clk, Clk_t, counter_1_ovf, counterpreset_1_ovf, decoder_1_out_0, decoder_1_out_1,
       decoder_1_out_2, decoder_1_out_3, delay_1_out, demultiplexer_1_out_0, demultiplexer_1_out_1,
       demultiplexer_1_out_2, demultiplexer_1_out_3, demultiplexer_1_out_4, demultiplexer_1_out_5,
       demultiplexer_1_out_6, demultiplexer_1_out_7, demultiplexer_1_out_8, demultiplexer_1_out_9,
       demultiplexer_1_out_10, demultiplexer_1_out_11, demultiplexer_1_out_12, demultiplexer_1_out_13,
       demultiplexer_1_out_14, demultiplexer_1_out_15, dipswitch_1_out, dipswitch_18_out, dipswitch_27_out,
       IR_In, IR_Out, JT_In, JT_Out, MA_In, MD_In, MD_Out, MP_In, nor_1_out, not_1_out, not_3_out, not_4_out,
       or_1_out, or_2_out, or_3_out, or_4_out, or_5_out, or_6_out, or_7_out, or_8_out, or_9_out, or_10_out,
       or_11_out, or_12_out, or_13_out, PC_In, PC_Inc, PC_Out, Reset_to_0_out, rs_ff_as_1_q, rs_ff_as_2_q,
       rs_ff_as_3_q, rs_ff_as_4_q, SC_Res, Set, Set_ALU, Set_AR, Set_Clk, Set_JMP, Set_MP, ShdwCpAct,
       Step_out;
  wire [0:0] multiplexer_2_out;
  wire [1:0] Jump_Mode_q;
  wire [2:0] Stp_Cnt_out;
  wire [3:0] register_1_q;
  wire [4:0] Mem_Page_q, Set_lookup_out;
  wire [5:0] Jump_Target_q, Mem_Addr_q, multiplexer_5_out, multiplexer_6_out, multiplexer_7_out,
       Next__no_jump_s, PC, Relative_s;
  wire [7:0] alu_1_outa, alu_1_outb, alu_1_q, Boot_ROM_d, Bus, dipswitch_19_out, GP_A_q, GP_B_q, GP_C_q,
       GP_D_q, GP_E_q, gpio8_1_dir_out, gpio8_1_val_out, gpio8_2_dir_out, gpio8_2_val_out, Inst_Reg_q,
       multiplexer_3_out;
  wire [10:0] counter_1_out, multiplexer_4_out;
  wire [15:0] dipswitch_2_out, Microcode_d, multiplexer_1_out;

  DipSwitch dipswitch_1 (.out(dipswitch_1_out));
  DipSwitch dipswitch_2 (.out(dipswitch_2_out[15]));
  DipSwitch dipswitch_3 (.out(dipswitch_2_out[14]));
  DipSwitch dipswitch_4 (.out(dipswitch_2_out[13]));
  DipSwitch dipswitch_5 (.out(dipswitch_2_out[12]));
  DipSwitch dipswitch_6 (.out(dipswitch_2_out[11]));
  DipSwitch dipswitch_7 (.out(dipswitch_2_out[10]));
  DipSwitch dipswitch_8 (.out(dipswitch_2_out[9]));
  DipSwitch dipswitch_9 (.out(dipswitch_2_out[8]));
  DipSwitch dipswitch_10 (.out(dipswitch_2_out[7]));
  DipSwitch dipswitch_11 (.out(dipswitch_2_out[6]));
  DipSwitch dipswitch_12 (.out(dipswitch_2_out[5]));
  DipSwitch dipswitch_13 (.out(dipswitch_2_out[4]));
  DipSwitch dipswitch_14 (.out(dipswitch_2_out[3]));
  DipSwitch dipswitch_15 (.out(dipswitch_2_out[2]));
  DipSwitch dipswitch_16 (.out(dipswitch_2_out[1]));
  DipSwitch dipswitch_17 (.out(dipswitch_2_out[0]));
  Register #(.Bits(8)) Inst_Reg (.D(Bus), .C(Clk), .en(IR_In), .Q(Inst_Reg_q));
  assign Bus = IR_Out ? Inst_Reg_q : 8'bz;  // Driver driver_1
  Multiplexer #(.Bits(16)) multiplexer_1 (
    .sel(dipswitch_1_out), .in_0(Microcode_d), .in_1(dipswitch_2_out), .out(multiplexer_1_out));
  LookUpTable #(.Bits(5)) Set_lookup (
    .in0(Bus[0]), .in1(Bus[1]), .in2(Bus[2]), .in3(Bus[3]), .in4(Bus[4]), .in5(Bus[5]), .out(Set_lookup_out));
  Register #(.Bits(4)) register_1 (.D(Bus[3:0]), .C(Clk), .en(Set_AR), .Q(register_1_q));
  LED Control_Overrides (.in(dipswitch_1_out));
  ROM #(.bigEndian("true"), .AddrBits(5), .Bits(16)) Microcode (
    .A({Inst_Reg_q[7:6], Stp_Cnt_out}), .sel(1'b1), .D(Microcode_d));
  Demultiplexer #(.Selector_Bits(4)) demultiplexer_1 (
    .sel(register_1_q), .in(AR_In), .out_0(demultiplexer_1_out_0), .out_1(demultiplexer_1_out_1),
    .out_2(demultiplexer_1_out_2), .out_3(demultiplexer_1_out_3), .out_4(demultiplexer_1_out_4),
    .out_5(demultiplexer_1_out_5), .out_6(demultiplexer_1_out_6), .out_7(demultiplexer_1_out_7),
    .out_8(demultiplexer_1_out_8), .out_9(demultiplexer_1_out_9), .out_10(demultiplexer_1_out_10),
    .out_11(demultiplexer_1_out_11), .out_12(demultiplexer_1_out_12), .out_13(demultiplexer_1_out_13),
    .out_14(demultiplexer_1_out_14), .out_15(demultiplexer_1_out_15));
  Multiplexer #(.Bits(16)) multiplexer_2 (
    .sel(ShdwCpAct), .in_0(multiplexer_1_out), .in_1({16{1'b0}}),
    .out({MP_In, MA_In, MD_In, MD_Out, AR_In, AR_Out, PC_Inc, PC_In, PC_Out, SC_Res, IR_In, IR_Out, JT_In, JT_Out, Set, multiplexer_2_out[0]}));
  assign {Set_MP, Set_AR, Set_JMP, Set_Clk, Set_ALU} = {5{Set}} & Set_lookup_out;  // And and_1, 5 bits wide
  Counter #(.Bits(3)) Stp_Cnt (.en(not_1_out), .C(Clk), .clr(SC_Res), .out(Stp_Cnt_out));  // open: ovf
  not not_1 (not_1_out, ShdwCpAct);
  and and_2 (and_2_out, decoder_1_out_0, Set_Clk);
  or or_1 (or_1_out, button_1_out, and_2_out);
  Button button_1 (.out(button_1_out));
  Button button_2 (.out(button_2_out));
  or or_2 (or_2_out, button_3_out, and_4_out);
  Button button_3 (.out(button_3_out));
  Button button_4 (.out(button_4_out));
  or or_3 (or_3_out, and_3_out, nor_1_out);
  and and_3 (and_3_out, decoder_1_out_1, Set_Clk);
  Decoder #(.Selector_Bits(2)) decoder_1 (
    .sel(Bus[1:0]), .out_0(decoder_1_out_0), .out_1(decoder_1_out_1), .out_2(decoder_1_out_2),
    .out_3(decoder_1_out_3));
  DipSwitch dipswitch_18 (.out(dipswitch_18_out));
  DipSwitch dipswitch_19 (.out(dipswitch_19_out[7]));
  DipSwitch dipswitch_20 (.out(dipswitch_19_out[6]));
  DipSwitch dipswitch_21 (.out(dipswitch_19_out[5]));
  DipSwitch dipswitch_22 (.out(dipswitch_19_out[4]));
  DipSwitch dipswitch_23 (.out(dipswitch_19_out[3]));
  DipSwitch dipswitch_24 (.out(dipswitch_19_out[2]));
  DipSwitch dipswitch_25 (.out(dipswitch_19_out[1]));
  DipSwitch dipswitch_26 (.out(dipswitch_19_out[0]));
  and and_4 (and_4_out, decoder_1_out_2, Set_Clk);
  LED led_1 (.in(Bus[7]));
  assign Bus = dipswitch_18_out ? dipswitch_19_out : 8'bz;  // Driver driver_2
  or or_4 (or_4_out, button_2_out, or_3_out);
  or or_5 (or_5_out, button_4_out, or_6_out);
  or or_6 (or_6_out, and_5_out, not_3_out);
  and and_5 (and_5_out, decoder_1_out_3, Set_Clk);
  LED led_2 (.in(Bus[6]));
  LED led_3 (.in(Bus[5]));
  Register #(.Bits(8)) GP_A (.D(Bus), .C(Clk), .en(demultiplexer_1_out_0), .Q(GP_A_q));
  Register #(.Bits(8)) GP_B (.D(Bus), .C(Clk), .en(demultiplexer_1_out_1), .Q(GP_B_q));
  Register #(.Bits(8)) GP_C (.D(Bus), .C(Clk), .en(demultiplexer_1_out_2), .Q(GP_C_q));
  Register #(.Bits(8)) GP_D (.D(Bus), .C(Clk), .en(demultiplexer_1_out_3), .Q(GP_D_q));
  Register #(.Bits(8)) GP_E (.D(Bus), .C(Clk), .en(demultiplexer_1_out_4), .Q(GP_E_q));
  ALU alu_1 (
    .DataIn(Bus), .Clk(Clk), .InA(demultiplexer_1_out_5), .InB(demultiplexer_1_out_6), .Mode(Set_ALU),
    .OutA(alu_1_outa), .OutB(alu_1_outb), .Q(alu_1_q));
  GPIO8 gpio8_1 (
    .Data_In(Bus), .Clk(Clk), .Dir(demultiplexer_1_out_9), .Val(demultiplexer_1_out_10),
    .Dir_Out(gpio8_1_dir_out), .Val_Out(gpio8_1_val_out));
  GPIO8 gpio8_2 (
    .Data_In(Bus), .Clk(Clk), .Dir(demultiplexer_1_out_11), .Val(demultiplexer_1_out_12),
    .Dir_Out(gpio8_2_dir_out), .Val_Out(gpio8_2_val_out));
  LED led_4 (.in(Bus[4]));
  LED led_5 (.in(Bus[3]));
  LED led_6 (.in(GP_A_q[7]));
  LED led_7 (.in(GP_B_q[7]));
  LED led_8 (.in(GP_C_q[7]));
  LED led_9 (.in(GP_D_q[7]));
  LED led_10 (.in(GP_E_q[7]));
  LED led_11 (.in(rs_ff_as_1_q));
  LED led_12 (.in(rs_ff_as_3_q));
  LED led_13 (.in(rs_ff_as_2_q));
  LED led_14 (.in(rs_ff_as_4_q));
  or or_7 (or_7_out, or_4_out, or_2_out, or_5_out);
  or or_8 (or_8_out, or_1_out, or_2_out, or_5_out);
  or or_9 (or_9_out, or_1_out, or_4_out, or_5_out);
  or or_10 (or_10_out, or_1_out, or_4_out, or_2_out);
  LED led_15 (.in(Bus[2]));
  LED led_16 (.in(Bus[1]));
  PullDown #(.Bits(8)) pulldown_1 (.out(Bus));
  LED led_17 (.in(GP_A_q[6]));
  LED led_18 (.in(GP_A_q[5]));
  LED led_19 (.in(GP_B_q[6]));
  LED led_20 (.in(GP_B_q[5]));
  LED led_21 (.in(GP_C_q[6]));
  LED led_22 (.in(GP_C_q[5]));
  LED led_23 (.in(GP_D_q[6]));
  LED led_24 (.in(GP_D_q[5]));
  LED led_25 (.in(GP_E_q[6]));
  LED led_26 (.in(GP_E_q[5]));
  LED led_27 (.in(gpio8_1_dir_out[7]));
  LED led_28 (.in(gpio8_1_val_out[7]));
  LED led_29 (.in(gpio8_2_dir_out[7]));
  LED led_30 (.in(gpio8_2_val_out[7]));
  RS_FF_AS rs_ff_as_1 (.S(or_1_out), .R(or_7_out), .Q(rs_ff_as_1_q));  // open: nQ
  RS_FF_AS rs_ff_as_2 (.S(or_2_out), .R(or_9_out), .Q(rs_ff_as_2_q));  // open: nQ
  LED led_31 (.in(Bus[0]));
  LED led_32 (.in(GP_A_q[4]));
  LED led_33 (.in(GP_A_q[3]));
  LED led_34 (.in(GP_B_q[4]));
  LED led_35 (.in(GP_B_q[3]));
  LED led_36 (.in(GP_C_q[4]));
  LED led_37 (.in(GP_C_q[3]));
  LED led_38 (.in(GP_D_q[4]));
  LED led_39 (.in(GP_D_q[3]));
  LED led_40 (.in(GP_E_q[4]));
  LED led_41 (.in(GP_E_q[3]));
  LED led_42 (.in(alu_1_outa[7]));
  LED led_43 (.in(alu_1_outa[6]));
  LED led_44 (.in(alu_1_outb[7]));
  LED led_45 (.in(alu_1_outb[6]));
  LED led_46 (.in(alu_1_q[7]));
  LED led_47 (.in(alu_1_q[6]));
  LED led_48 (.in(gpio8_1_dir_out[6]));
  LED led_49 (.in(gpio8_1_dir_out[5]));
  LED led_50 (.in(gpio8_1_val_out[6]));
  LED led_51 (.in(gpio8_1_val_out[5]));
  LED led_52 (.in(gpio8_2_dir_out[6]));
  LED led_53 (.in(gpio8_2_dir_out[5]));
  LED led_54 (.in(gpio8_2_val_out[6]));
  LED led_55 (.in(gpio8_2_val_out[5]));
  Button Step (.out(Step_out));
  Seven_Seg_Hex seven_seg_hex_1 (.d(Bus[7:4]), .dp(1'b0));
  LED led_56 (.in(GP_A_q[2]));
  LED led_57 (.in(GP_A_q[1]));
  LED led_58 (.in(GP_B_q[2]));
  LED led_59 (.in(GP_B_q[1]));
  LED led_60 (.in(GP_C_q[2]));
  LED led_61 (.in(GP_C_q[1]));
  LED led_62 (.in(GP_D_q[2]));
  LED led_63 (.in(GP_D_q[1]));
  LED led_64 (.in(GP_E_q[2]));
  LED led_65 (.in(GP_E_q[1]));
  LED led_66 (.in(alu_1_outa[5]));
  LED led_67 (.in(alu_1_outa[4]));
  LED led_68 (.in(alu_1_outb[5]));
  LED led_69 (.in(alu_1_outb[4]));
  LED led_70 (.in(alu_1_q[5]));
  LED led_71 (.in(alu_1_q[4]));
  LED led_72 (.in(gpio8_1_dir_out[4]));
  LED led_73 (.in(gpio8_1_dir_out[3]));
  LED led_74 (.in(gpio8_1_val_out[4]));
  LED led_75 (.in(gpio8_1_val_out[3]));
  LED led_76 (.in(gpio8_2_dir_out[4]));
  LED led_77 (.in(gpio8_2_dir_out[3]));
  LED led_78 (.in(gpio8_2_val_out[4]));
  LED led_79 (.in(gpio8_2_val_out[3]));
  assign Clk = rs_ff_as_1_q ? 1'b0 : 1'bz;  // Driver driver_3
  assign Clk = rs_ff_as_2_q ? Slow : 1'bz;  // Driver driver_4
  RS_FF_AS rs_ff_as_3 (.S(or_4_out), .R(or_8_out), .Q(rs_ff_as_3_q));  // open: nQ
  RS_FF_AS rs_ff_as_4 (.S(or_5_out), .R(or_10_out), .Q(rs_ff_as_4_q));  // open: nQ
  Seven_Seg_Hex seven_seg_hex_2 (.d(Bus[3:0]), .dp(1'b0));
  LED led_80 (.in(GP_A_q[0]));
  LED led_81 (.in(GP_B_q[0]));
  LED led_82 (.in(GP_C_q[0]));
  LED led_83 (.in(GP_D_q[0]));
  LED led_84 (.in(GP_E_q[0]));
  LED led_85 (.in(alu_1_outa[3]));
  LED led_86 (.in(alu_1_outa[2]));
  LED led_87 (.in(alu_1_outb[3]));
  LED led_88 (.in(alu_1_outb[2]));
  LED led_89 (.in(alu_1_q[3]));
  LED led_90 (.in(alu_1_q[2]));
  LED led_91 (.in(gpio8_1_dir_out[2]));
  LED led_92 (.in(gpio8_1_dir_out[1]));
  LED led_93 (.in(gpio8_1_val_out[2]));
  LED led_94 (.in(gpio8_1_val_out[1]));
  LED led_95 (.in(gpio8_2_dir_out[2]));
  LED led_96 (.in(gpio8_2_dir_out[1]));
  LED led_97 (.in(gpio8_2_val_out[2]));
  LED led_98 (.in(gpio8_2_val_out[1]));
  assign Clk = rs_ff_as_3_q ? Step_out : 1'bz;  // Driver driver_5
  assign Clk = rs_ff_as_4_q ? Fast : 1'bz;  // Driver driver_6
  LED led_99 (.in(alu_1_outa[1]));
  LED led_100 (.in(alu_1_outa[0]));
  LED led_101 (.in(alu_1_outb[1]));
  LED led_102 (.in(alu_1_outb[0]));
  LED led_103 (.in(alu_1_q[1]));
  LED led_104 (.in(alu_1_q[0]));
  LED led_105 (.in(gpio8_1_dir_out[0]));
  LED led_106 (.in(gpio8_1_val_out[0]));
  LED led_107 (.in(gpio8_2_dir_out[0]));
  LED led_108 (.in(gpio8_2_val_out[0]));
  PullDown pulldown_2 (.out(Clk));
  not not_2 (Clk_t, Clk);
  or or_11 (or_11_out, or_11_out, Clk);
  not not_3 (not_3_out, or_11_out);
  Button Reset_to_0 (.out(Reset_to_0_out));
  PullDown pulldown_3 (.out(or_11_out));
  Delay #(.delayTime(5)) delay_1 (.in(ShdwCpAct), .out(delay_1_out));
  not not_4 (not_4_out, delay_1_out);
  nor nor_1 (nor_1_out, ShdwCpAct, not_4_out);
  CounterPreset #(.Bits(6)) counterpreset_1 (
    .en(PC_Inc), .C(Clk), .dir(1'b0), .in(Bus[5:0]), .ld(PC_In), .clr(Reset_to_0_out), .out(PC),
    .ovf(counterpreset_1_ovf));
  LED Overflow (.in(counterpreset_1_ovf));
  Counter #(.Bits(11)) counter_1 (.en(ShdwCpAct), .C(Clk), .clr(1'b0), .out(counter_1_out), .ovf(counter_1_ovf));
  PullDown pulldown_4 (.out(counter_1_ovf));
  assign Bus = PC_Out ? {2'b00, PC} : 8'bz;  // Driver driver_7
  Multiplexer #(.Selector_Bits(4), .Bits(8)) multiplexer_3 (
    .sel(register_1_q), .in_0(GP_A_q), .in_1(GP_B_q), .in_2(GP_C_q), .in_3(GP_D_q), .in_4(GP_E_q),
    .in_5(alu_1_outa), .in_6(alu_1_outb), .in_7(alu_1_q), .in_8({8{1'b0}}), .in_9(gpio8_1_dir_out),
    .in_10(gpio8_1_val_out), .in_11(gpio8_2_dir_out), .in_12(gpio8_2_val_out), .in_13({8{1'b0}}),
    .in_14({8{1'b0}}), .in_15({8{1'b0}}), .out(multiplexer_3_out));
  Register #(.Bits(5)) Mem_Page (.D(Bus[4:0]), .C(Clk), .en(MP_In), .Q(Mem_Page_q));
  Register #(.Bits(6)) Mem_Addr (.D(Bus[5:0]), .C(Clk), .en(MA_In), .Q(Mem_Addr_q));
  or or_12 (or_12_out, counter_1_ovf, or_12_out);
  PullDown pulldown_5 (.out(or_12_out));
  assign Bus = AR_Out ? multiplexer_3_out : 8'bz;  // Driver driver_8
  ROM #(.AddrBits(11), .Bits(8)) Boot_ROM (.A(counter_1_out), .sel(ShdwCpAct), .D(Boot_ROM_d));
  Seven_Seg_Hex seven_seg_hex_3 (.d({2'b00, PC[5:4]}), .dp(1'b0));
  Seven_Seg_Hex seven_seg_hex_4 (.d({3'b000, Mem_Page_q[4]}), .dp(1'b0));
  Multiplexer #(.Bits(11)) multiplexer_4 (
    .sel(ShdwCpAct), .in_0({{5{1'b0}}, Mem_Addr_q}), .in_1(counter_1_out), .out(multiplexer_4_out));
  not not_5 (ShdwCpAct, or_12_out);
  Seven_Seg_Hex seven_seg_hex_5 (.d(PC[3:0]), .dp(1'b0));
  Seven_Seg_Hex seven_seg_hex_6 (.d(Mem_Page_q[3:0]), .dp(1'b0));
  // Probe Address on multiplexer_4_out
  assign Bus = ShdwCpAct ? Boot_ROM_d : 8'bz;  // Driver driver_9
  Seven_Seg_Hex seven_seg_hex_7 (.d({2'b00, Mem_Addr_q[5:4]}), .dp(1'b0));
  or or_13 (or_13_out, MD_In, ShdwCpAct);
  Seven_Seg_Hex seven_seg_hex_8 (.d(Mem_Addr_q[3:0]), .dp(1'b0));
  RAMSinglePort #(.AddrBits(11), .Bits(8)) ramsingleport_1 (
    .A(multiplexer_4_out), .str(or_13_out), .C(Clk), .ld(MD_Out), .D(Bus));
  // Probe Data on Bus
  Register #(.Bits(2)) Jump_Mode (.D(Bus[1:0]), .C(Clk), .en(Set_JMP), .Q(Jump_Mode_q));
  Register #(.Bits(6)) Jump_Target (.D(Bus[5:0]), .C(Clk), .en(JT_In), .Q(Jump_Target_q));
  Add #(.Bits(6)) Next__no_jump (.a(PC), .b(6'b000001), .c_i(1'b0), .s(Next__no_jump_s));  // open: c_o
  Add #(.Bits(6)) Relative (.a(PC), .b(Jump_Target_q), .c_i(1'b0), .s(Relative_s));  // open: c_o
  Multiplexer #(.Bits(6)) multiplexer_5 (
    .sel(dipswitch_27_out), .in_0(Jump_Target_q), .in_1(Next__no_jump_s), .out(multiplexer_5_out));
  DipSwitch dipswitch_27 (.out(dipswitch_27_out));
  Multiplexer #(.Bits(6)) multiplexer_6 (
    .sel(dipswitch_27_out), .in_0(Next__no_jump_s), .in_1(Jump_Target_q), .out(multiplexer_6_out));
  Multiplexer #(.Selector_Bits(2), .Bits(6)) multiplexer_7 (
    .sel(Jump_Mode_q), .in_0(Jump_Target_q), .in_1(multiplexer_6_out), .in_2(multiplexer_5_out),
    .in_3(Relative_s), .out(multiplexer_7_out));
  assign Bus = JT_Out ? {2'b00, multiplexer_7_out} : 8'bz;  // Driver driver_10

  // Notes on the sheet:
  //   Slow: Hz: 5
  //   Fast: Hz: 500
  //   Control
  //   Set Logic
  //   AR_Sel Logic
  //   contents of Set_lookup (hex, n*v repeats v):
  //   8*1,4*2,4*4,16*8,32*10
  //   Microcode loads Microcode.bin
  //   Clock
  //   Software Select
  //   Bus
  //   GP Registers
  //   ALU
  //   Flags Register
  //   Mode latching
  //   Program Counter
  //   Poweron Select
  //   Memory
  //   Boot_ROM loads Boot.bin
  //   Mem Page
  //   Mem Addr
  //   ALU result boolean
endmodule
