// Digital circuit GPIO8.dig as structural Verilog
module GPIO8 (
  input  [7:0] Data_In,
  input  Clk,
  input  Dir,
  input  Val,
  output [7:0] Dir_Out,
  output [7:0] Val_Out
);

  Register #(.Bits(8)) register_1 (.D(Data_In), .C(Clk), .en(Dir), .Q(Dir_Out));
  Register #(.Bits(8)) register_2 (.D(Data_In), .C(Clk), .en(Val), .Q(Val_Out));
endmodule
