// Digital circuit fullAdder.dig as structural Verilog
module fullAdder (
  input  A,
  input  B,
  input  Ci,
  output S,
  output Co
);

  wire halfadder_1_c, halfadder_1_s, halfadder_2_c;

  halfAdder halfadder_1 (.A(A), .B(B), .S(halfadder_1_s), .C(halfadder_1_c));
  halfAdder halfadder_2 (.A(Ci), .B(halfadder_1_s), .S(S), .C(halfadder_2_c));
  xor xor_1 (Co, halfadder_2_c, halfadder_1_c);
endmodule
